# Fritzing sketch CO2_Ampel (saved by Fritzing 0.9.10b)
breadboards: 1

parts:
  Part1 = MPL3115A2 I2C Barometric Pressure, Altitude, Temperature Sensor
  Part2 = Adafruit CCS811
  WeMos_D1_Mini1 = WeMos D1 Mini
  Part3 = Adafruit Breadboard-Friendly NeoPixel [part_number="Adafruit #1312"]
  A1 = Waveshare e-Paper HAT [package=THT]

nets:
  VIN: Part1.VIN, Part2.VIN, WeMos_D1_Mini1.3V3, A1.pin_8
  GND: Part1.GND, Part2.GND, WeMos_D1_Mini1.G, Part3.GND, A1.pin_7
  N1: Part1.SCL, Part2.SCL, WeMos_D1_Mini1.D2
  N2: Part1.SDA, Part2.SDA, WeMos_D1_Mini1.D1
  5V: WeMos_D1_Mini1.5V, Part3.VDD
  N3: WeMos_D1_Mini1.D0, A1.pin_2
  N4: WeMos_D1_Mini1.D3, A1.pin_3
  N5: WeMos_D1_Mini1.D4, Part3.IN
  N6: WeMos_D1_Mini1.D5, A1.pin_5
  N7: WeMos_D1_Mini1.D6, A1.pin_1
  N8: WeMos_D1_Mini1.D7, A1.pin_6
  N9: WeMos_D1_Mini1.D8, A1.pin_4

custom parts:
  MPL3115A2 I2C Barometric Pressure, Altitude, Temperature Sensor: This pressure sensor from Freescale is a great low-cost sensing solution for precision measurement of barometric pressure and altitude. The MPL3115A2 has a typical 1.5 Pascal resolution, which can resolve altitude at 0.3 meters (compare to the BMP180 which can do 0.17m). It has some upsides compared to the BMP180, such as interrupt outputs for ultra-low power usage, and its also a heck of a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
  Adafruit Breadboard-Friendly NeoPixel: This is the easiest way possible to add small, bright RGB pixels to your project. We took the same technology from our Flora NeoPixels and made them breadboard friendly, with two rows of 3 x 0.1" spaced header on each side for easy soldering, chaining and breadboarding. These ultra-bright LEDs have a constant-current driver cooked right into the LED package! The pixels are chainable - so you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
  Waveshare e-Paper HAT: .This is a universal driver board for e-Paper raw panels, can be used to drive various SPI interface e-Paper from Waveshare.
